# Fritzing sketch autogo-fritzing (saved by Fritzing 0.9.9b)
circuit board: 8.46667cm x 5.64444cm
breadboards: 1

parts:
  Mod1 = Raspberry Pi 4B
  Componente1 = Arduino Uno (Rev3)
  PWM1 = PCA9685 16x12-bit PWM Breakout
  L298N1 = L298N DC motor driver
  M1 = gear-motor
  M2 = gear-motor
  Componente2 = HC-SR04
  Componente3 = HC-SR04
  Componente4 = HC-SR04
  Componente5 = HC-SR04
  CAMERA1 = TTL Serial JPEG Camera  # not connected
  J2 = Basic Servo
  J3 = Basic Servo
  F2 = Fan - Ventilador [package=THT]
  LCD2 = LCD screen
  LCM1602_IIC2 = LCM1602 IIC [part_number="LCM1602 IIC" chip_label="LCM1602 IIC" package="DIP (Dual Inline) [THT]"]
  VCC2 = 4 x AAA Battery Mount

nets (from the breadboard view):
  N1: Mod1.3V3, PWM1.no_name_yet#505
  5V: Mod1.5V, F2.5V, LCM1602_IIC2.VCC
  N2: Mod1.GPIO2, Componente1.A4/SDA
  GND: Mod1.GPIO3, Mod1.GND, Componente1.A5/SCL, Componente1.GND, PWM1.no_name_yet#501, PWM1.no_name_yet#701, PWM1.no_name_yet#1000, PWM1.no_name_yet#1001, L298N1.GND, Componente2.Gnd, Componente3.Gnd, Componente4.Gnd, Componente5.Gnd, J2.gnd, J3.gnd, F2.GND, LCM1602_IIC2.GND, VCC2.-
  N3: Mod1.GPIO17, L298N1.IN1
  N4: Mod1.GPIO18, L298N1.ENA
  N5: Mod1.GPIO22, L298N1.IN2
  N6: Mod1.GPIO23, L298N1.IN3
  N7: Mod1.GPIO7, LCM1602_IIC2.SCL
  N8: Mod1.GPIO6, LCM1602_IIC2.SDA
  N9: Mod1.GPIO12, PWM1.no_name_yet#504
  N10: Mod1.GPIO13, PWM1.no_name_yet#503
  N11: Mod1.GPIO19, L298N1.ENB
  N12: Componente1.D8, Componente3.Echo
  N13: Componente1.D9_PWM, Componente3.Trig
  N14: Componente1.D2, Componente4.Trig
  N15: Componente1.D3_PWM, Componente4.Echo
  N16: Componente1.D4, Componente2.Trig
  N17: Componente1.D5_PWM, Componente2.Echo
  N18: Componente1.D6_PWM, Componente5.Echo
  N19: Componente1.D7, Componente5.Trig
  VCC: Componente1.VIN, PWM1.no_name_yet#100, PWM1.no_name_yet#101, PWM1.no_name_yet#706, Componente2.Vcc, Componente3.Vcc, Componente4.Vcc, Componente5.Vcc, J2.vcc, J3.vcc
  N20: PWM1.no_name_yet#0, J2.pulse
  N21: PWM1.no_name_yet#1, J3.pulse
  N22: L298N1.OUT1, M2.pin_2
  N23: L298N1.OUT2, M2.pin_1
  N24: L298N1.OUT3, M1.pin_2
  N25: L298N1.OUT4, M1.pin_1
  N26: L298N1.12V, VCC2.+
  VSS: LCD2.VSS, LCM1602_IIC2.VSS
  VDD: LCD2.VDD, LCM1602_IIC2.VDD
  N27: LCD2.V0, LCM1602_IIC2.V0
  N28: LCD2.RS, LCM1602_IIC2.RS
  N29: LCD2.R/W, LCM1602_IIC2.RW
  N30: LCD2.E, LCM1602_IIC2.E
  N31: LCD2.DB0, LCM1602_IIC2.D0
  N32: LCD2.DB1, LCM1602_IIC2.D1
  N33: LCD2.DB2, LCM1602_IIC2.D2
  N34: LCD2.DB3, LCM1602_IIC2.D3
  N35: LCD2.DB4, LCM1602_IIC2.D4
  N36: LCD2.DB5, LCM1602_IIC2.D5
  N37: LCD2.DB6, LCM1602_IIC2.D6
  N38: LCD2.DB7, LCM1602_IIC2.D7
  N39: LCD2.LED+, LCM1602_IIC2.A
  N40: LCD2.LED-, LCM1602_IIC2.K
  N41: LCM1602_IIC2.LED_A, LCM1602_IIC2.LED_B

custom parts:
  L298N DC motor driver: 2x DC motor driver with 78M05 positive voltage regulator (7..35 V) L298N: max 46 V, 2 A Set 5 V Enable jumper to enable 5 V regultor (needed for the L298N) and +5 V output at screw terminal or supply external +5 V at screw terminal Set ENA and/or ENB to +5 V to enable motor permanently or supply ENA and/or ENB with PWM signal IN1 and IN2 set rotation directory for motor A (OUT1/OUT2) IN2 and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
  HC-SR04: HC-SR04 ultrasonic distance sensor
  TTL Serial JPEG Camera: TTL Serial JPEG Camera with NTSC Out
  Fan - Ventilador: Ventilador de 2 pines, se encuentra comunmente en computadoras de escritorio
  LCM1602 IIC: I2C-Module to use a 1602 or 2004 LCD on with the wire.h libory Serial LCD Modul
